# Fritzing sketch diyshift_barebones (saved by Fritzing 0.5.2b)
breadboards: 1

parts:
  Arduino1 = Arduino
  S1 = Pushbutton [package="[THT]"]
  S2 = Pushbutton [package="[THT]"]
  Q1 = Basic FET N-Channel [package="TO220 [THT]"]
  R1 = Resistor [resistance=10k package=THT]
  R2 = Resistor [resistance=10k package=THT]
  LED1 = Red LED - 5mm [package="5 mm [THT]"]
  R3 = Resistor [resistance=220 package=THT]
  J1 = Basic Servo
  S3 = Toggle Switch [package=THT]

nets:
  GND: Arduino1.GND, Q1.source, R1.Pin_1, R2.Pin_1, LED1.cathode, S3.COM
  N1: Arduino1.D13, R3.Pin_1
  N2: Arduino1.D9, J1.pulse
  N3: Arduino1.D8, S3.L2
  N4: Arduino1.D7, Q1.gate
  N5: Arduino1.D3, S2.Pin_3, S2.Pin_4, R2.Pin_0
  N6: Arduino1.D2, S1.Pin_3, S1.Pin_4, R1.Pin_0
  +5V: Arduino1.+5V, S1.Pin_1, S1.Pin_2, S2.Pin_1, S2.Pin_2, J1.vcc
  N7: Q1.drain, J1.gnd
  N8: LED1.anode, R3.Pin_0
